// Logisim project 4bit-shift-register.circ as structural Verilog: 1 circuit, main circuit main
module main (
  input  D,
  input  Clear,
  input  Enable,
  input  Preset,
  output out_5,
  output out_6,
  output out_7,
  output out_8,
  output Q
);

  wire Clock_out;

  Clock Clock (.out(Clock_out));
  D_Flip_Flop d_ff_1 (.clk(Clock_out), .D(D), .Q(out_5), .preset(Preset), .en(Enable), .reset(Clear));  // open: Qn
  D_Flip_Flop d_ff_2 (.clk(Clock_out), .D(out_5), .Q(out_6), .preset(Preset), .en(Enable), .reset(Clear));  // open: Qn
  D_Flip_Flop d_ff_3 (.clk(Clock_out), .D(out_6), .Q(out_7), .preset(Preset), .en(Enable), .reset(Clear));  // open: Qn
  D_Flip_Flop d_ff_4 (.clk(Clock_out), .D(out_7), .Q(out_8), .preset(Preset), .en(Enable), .reset(Clear));  // open: Qn

  assign Q = out_8;
endmodule
